// Logisim project traffic-light-system.circ as structural Verilog: 4 circuits, main circuit System v1.0
module System_v1_0 (
  input  Signal,
  input  Zero
);

  wire clock_1_out, G1, G2, G3, G4, PG1, PG2, PG3, PG4, PR1, PR2, PR3, PR4, R1, R2, R3, R4, Y1, Y2, Y3, Y4;
  wire [1:0] E, N, S, W;
  wire [3:0] n4_bit_counter_1_out_4;

  Clock clock_1 (.out(clock_1_out));
  traffic_signal traffic_signal_1 (.in_1(N), .out_2(R3), .out_3(Y3), .out_4(G3), .out_5(PR3), .out_6(PG3));
  traffic_signal traffic_signal_2 (.in_1(E), .out_2(R2), .out_3(Y2), .out_4(G2), .out_5(PR2), .out_6(PG2));
  _4_bit_counter u_4_bit_counter_1 (
    .Power(Signal), .Zero(Zero), .out_4(n4_bit_counter_1_out_4[0]), .out_5(n4_bit_counter_1_out_4[1]),
    .out_6(n4_bit_counter_1_out_4[2]), .out_7(n4_bit_counter_1_out_4[3]), .Clock(clock_1_out));
  traffic_signal traffic_signal_3 (.in_1(W), .out_2(R4), .out_3(Y4), .out_4(G4), .out_5(PR4), .out_6(PG4));
  traffic_signal traffic_signal_4 (.in_1(S), .out_2(R1), .out_3(Y1), .out_4(G1), .out_5(PR1), .out_6(PG1));
  Hex_Digit_Display hex_digit_display_1 (.value(n4_bit_counter_1_out_4));  // open: dp
  controller controller_1 (.in_1(n4_bit_counter_1_out_4), .South(S), .East(E), .North(N), .West(W));
  LED led_1 (.in(R4));
  LED led_2 (.in(Y4));
  LED led_3 (.in(G4));
  LED led_4 (.in(G4));
  LED led_5 (.in(PR3));
  LED led_6 (.in(PG3));
  LED led_7 (.in(G3));
  LED led_8 (.in(Y3));
  LED led_9 (.in(R3));
  LED led_10 (.in(G3));
  LED led_11 (.in(PR2));
  LED led_12 (.in(PG2));
  LED led_13 (.in(PR4));
  LED led_14 (.in(PG4));
  LED led_15 (.in(Y1));
  LED led_16 (.in(G1));
  LED led_17 (.in(G1));
  LED led_18 (.in(R1));
  LED led_19 (.in(PR1));
  LED led_20 (.in(PG1));
  LED led_21 (.in(G2));
  LED led_22 (.in(G2));
  LED led_23 (.in(Y2));
  LED led_24 (.in(R2));

  // Notes on the sheet:
  //   Clock
  //   NORTH
  //   EAST
  //   Control Circuit
  //   System v1.0.0
  //   Released on May 28, 2021
  //   Copyright (c) 2021 Capella87
  //   github.com/Capella87/traffic-light-crossroads
  //   WEST
  //   SOUTH
  //   WEST
  //   Traffic Light System in crossroad
  //   NORTH
  //   SOUTH
  //   EAST
endmodule

module _4_bit_counter (
  input  Power,
  input  Zero,
  input  Clock,
  output out_4,
  output out_5,
  output out_6,
  output out_7
);

  wire and_1_out, and_2_out, not_1_out;

  not not_1 (not_1_out, Clock);
  J_K_Flip_Flop j_k_ff_1 (.J(Power), .clk(not_1_out), .K(Power), .Q(out_4), .reset(Zero));  // open: Qn, preset, en
  and and_1 (and_1_out, out_4, out_5);
  J_K_Flip_Flop j_k_ff_2 (
    .J(out_4), .clk(not_1_out), .K(out_4), .Q(out_5), .en(Power), .reset(Zero));  // open: Qn, preset
  J_K_Flip_Flop j_k_ff_3 (
    .J(and_1_out), .clk(not_1_out), .K(and_1_out), .Q(out_6), .en(Power), .reset(Zero));  // open: Qn, preset
  and and_2 (and_2_out, out_4, out_5, out_6);
  J_K_Flip_Flop j_k_ff_4 (
    .J(and_2_out), .clk(not_1_out), .K(and_2_out), .Q(out_7), .en(Power), .reset(Zero));  // open: Qn, preset
endmodule

module controller (
  input  [3:0] in_1,
  output [1:0] South,
  output [1:0] East,
  output [1:0] North,
  output [1:0] West
);

  wire not_1_out, not_2_out, not_3_out, not_4_out, not_5_out, not_6_out, not_7_out, or_1_out;

  not not_1 (not_1_out, in_1[3]);
  not not_2 (not_2_out, in_1[2]);
  not not_3 (not_3_out, in_1[1]);
  or or_1 (or_1_out, not_3_out, not_4_out);
  not not_4 (not_4_out, in_1[0]);
  not not_5 (not_5_out, in_1[3]);
  not not_6 (not_6_out, in_1[2]);
  not not_7 (not_7_out, in_1[2]);
  and and_1 (South[0], in_1[0], in_1[1], not_1_out, not_2_out);
  and and_2 (South[1], not_1_out, not_2_out, or_1_out);
  and and_3 (East[0], not_5_out, in_1[2], in_1[1], in_1[0]);
  and and_4 (East[1], not_5_out, in_1[2], or_1_out);
  and and_5 (North[0], in_1[3], not_6_out, in_1[1], in_1[0]);
  and and_6 (North[1], in_1[3], not_7_out, or_1_out);
  and and_7 (West[0], in_1[3], in_1[2], in_1[1], in_1[0]);
  and and_8 (West[1], in_1[3], in_1[2], or_1_out);
endmodule

module traffic_signal (
  input  [1:0] in_1,
  output out_2,
  output out_3,
  output out_4,
  output out_5,
  output out_6
);

  nor nor_1 (out_2, in_1[0], in_1[1]);
  or or_1 (out_5, out_2, in_1[0]);
  LED led_1 (.in(out_2));
  LED led_2 (.in(in_1[0]));
  LED led_3 (.in(in_1[1]));
  LED led_4 (.in(in_1[1]));
  LED led_5 (.in(out_5));
  LED led_6 (.in(in_1[1]));

  assign out_3 = in_1[0];
  assign out_4 = in_1[1];
  assign out_6 = in_1[1];

  // Other names for the same wires on the sheet: Y = in_1[0]; G = in_1[1]; PG = in_1[1]; PR = out_5; R = out_2
endmodule
